# Fritzing sketch Untitled Sketch (saved by Fritzing 0.8.3b)
circuit board: 16.9333cm x 5.64444cm
breadboards: 1

parts:
  Bauteil1 = Arduino Uno (Rev3)
  Q1 = PNP-Transistor [package="TO92 [THT]"]
  Q2 = PNP-Transistor [package="TO92 [THT]"]
  Q3 = PNP-Transistor [package="TO92 [THT]"]
  Q4 = PNP-Transistor [package="TO92 [THT]"]
  R1 = Resistor [tolerance=±5% resistance=1k package=THT]
  R2 = Resistor [tolerance=±5% resistance=1k package=THT]
  R3 = Resistor [tolerance=±5% resistance=1k package=THT]
  R4 = Resistor [tolerance=±5% resistance=1k package=THT]
  S1 = Pushbutton [package="[THT]"]
  S2 = Pushbutton [package="[THT]"]
  S3 = Pushbutton [package="[THT]"]
  S4 = Pushbutton [package="[THT]"]
  VCC1 = Battery
  LED1 = LED - 5mm [color="Red (633nm)" package="5 mm [THT]"]

nets:
  N1: Bauteil1.GND, VCC1.-, LED1.cathode
  N2: Bauteil1.D8, R4.Pin_0
  N3: Bauteil1.D9_PWM, R3.Pin_0
  N4: Bauteil1.D10_PWM/SS, R2.Pin_0
  N5: Bauteil1.D11_PWM/MOSI, R1.Pin_0
  N6: Bauteil1.D12/MISO, VCC1.+, LED1.anode
  N7: Q1.E, S1.Pin_3, S1.Pin_4
  N8: Q1.B, R1.Pin_1
  N9: Q1.C, S1.Pin_2
  N10: Q2.E, S2.Pin_4
  N11: Q2.B, R2.Pin_1
  N12: Q2.C, S2.Pin_2
  N13: Q3.E, S3.Pin_4
  N14: Q3.B, R3.Pin_1
  N15: Q3.C, S3.Pin_2
  N16: Q4.E, S4.Pin_4
  N17: Q4.B, R4.Pin_1
  N18: Q4.C, S4.Pin_2
